// Digital circuit ALU.dig as structural Verilog
module ALU (
);

  ALU_CU alu_cu_1 ();  // open: BGN, RST, CLK, CNT7, Q0, Q_1, A7, OP, c0, c0_2, c1, c2, c3, c4, cR, cL, c5, c7, c8, c6, c7_5
endmodule
